# Fritzing sketch RFID-open-door (saved by Fritzing 0.9.0b)
breadboards: 1

parts:
  RFID1 = RFID Reader
  Componente1 = Arduino Uno (Rev3)
  R2 = Resistor [tolerance=±5% resistance=1M package=THT]
  R4 = Resistor [tolerance=±5% resistance=220 package=THT]
  R5 = Resistor [tolerance=±5% resistance=10k package=THT]
  LCD1 = LCD screen
  R6 = Resistor [tolerance=±5% resistance=220 package=THT]
  D1 = Rectifier Diode [part_number=1N4001 package="300 mil [THT]"]
  U1 = Optocoupler [package=THT]
  U2 = Optocoupler [package=THT]
  R7 = Resistor [tolerance=±5% resistance=220 package=THT]
  R8 = Resistor [tolerance=±5% resistance=220 package=THT]
  S5 = Pushbutton [package="[THT]"]
  S6 = Pushbutton [package="[THT]"]
  S7 = Pushbutton [package="[THT]"]
  S8 = Pushbutton [package="[THT]"]
  R9 = Resistor [tolerance=±5% resistance=10k package=THT]
  C1 = Electrolytic Capacitor [capacitance=0.1mF voltage=6.3V package="100 mil [THT, electrolytic]"]

nets:
  GND: RFID1.RES, Componente1.GND, LCD1.VSS, LCD1.V0, LCD1.R/W, LCD1.LED-, U1.Pin_2, U1.Pin_5, R8.Pin_1, R9.Pin_1, C1.-
  N1: RFID1.D0, Componente1.D0/RX
  +5V: RFID1.+5V, Componente1.5V, R2.Pin_0, R4.Pin_0, R5.Pin_0, LCD1.VDD, S5.Pin_2, C1.+
  N2: Componente1.A0, S5.Pin_4, S6.Pin_3, S6.Pin_4, S7.Pin_4, S8.Pin_4, R9.Pin_0
  N3: Componente1.D8, U1.Pin_4
  N4: Componente1.D11_PWM/MOSI, LCD1.RS
  N5: Componente1.D12/MISO, LCD1.E
  N6: Componente1.D2, U2.Pin_1
  N7: Componente1.D3_PWM, R6.Pin_0
  N8: Componente1.D4, LCD1.DB4
  N9: Componente1.D5_PWM, LCD1.DB5
  N10: Componente1.D6_PWM, LCD1.DB6
  N11: Componente1.D7, LCD1.DB7
  N12: R2.Pin_1, S8.Pin_1, S8.Pin_2
  N13: R4.Pin_1, S6.Pin_1, S6.Pin_2
  N14: R5.Pin_1, S7.Pin_1, S7.Pin_2
  N15: LCD1.LED+, R6.Pin_1
  N16: D1.anode, R7.Pin_1
  N17: U1.Pin_1, R7.Pin_0
  N18: U2.Pin_2, R8.Pin_0

notes:
  Citofono
  Alimentatore citofono 12VAC
  (o altra compatibile)
  Portone
